# Fritzing sketch fritzing (saved by Fritzing 0.9.3b)
breadboards: 1

parts:
  R7 = Resistor [tolerance=±5% resistance=220 package="0402 [SMD]"]
  LED1 = smd LED [color="Green (570nm)" package="0805 [SMD]"]
  R8 = Resistor [tolerance=±5% resistance=10k package="0805 [SMD]"]
  R9 = Resistor [tolerance=±5% resistance=1k package="0805 [SMD]"]
  R10 = Resistor [tolerance=±5% resistance=10k package="0805 [SMD]"]
  Q1 = NPN-Transistor [package="TO92 [THT]"]
  RHT1 = Humidity and Temperature Sensor RHT03
  U1 = NodeMCU V3.0
  KY-1 = Keyes Relay [package=THT]
  R11 = Photocell (LDR) [package=THT]
  R12 = Resistor [tolerance=±5% resistance=220 package="0402 [SMD]"]
  LED2 = smd LED [color="Red (633nm)" package="0805 [SMD]"]
  R13 = Resistor [tolerance=±5% resistance=10k package="0805 [SMD]"]

nets:
  N1: R7.Pin_0, LED1.anode
  N2: R7.Pin_1, U1.D3
  N3: LED1.cathode, U1.GND, KY-1.ground, R12.Pin_0, R13.Pin_1
  N4: R8.Pin_0, Q1.B
  N5: R8.Pin_1, U1.D6
  N6: R9.Pin_0, Q1.C, KY-1.signal
  N7: R9.Pin_1, U1.Vin, KY-1.power, R11.pin_0
  N8: R10.Pin_0, RHT1.Data-signal, U1.D5
  VCC: R10.Pin_1, RHT1.Vcc, U1.3V3
  N9: U1.D1, R11.pin_1, R13.Pin_0
  N10: U1.D8, LED2.anode
  N11: R12.Pin_1, LED2.cathode

custom parts:
  NodeMCU V3.0: NodeMcu V3 Lua WIFI Development Board
  Keyes Relay: The Keyes 5V relay module is suitable for SCM development, home appliance control. It uses a 5V~12V TIL control signal which can control DC / AC signal.
